// Logisim project 16-bit ALU.circ as structural Verilog
// 1- bit
module _1_bit_ALU (
  input  A,
  input  B,
  input  [2:0] Operation,
  input  Cin,
  input  Sub,
  output Result,
  output Cout
);

  wire adder_1_out, AND_out, nor_1_out, OR_out, xor_1_out;

  xor xor_1 (xor_1_out, B, Sub);
  and AND (AND_out, A, B);
  or OR (OR_out, A, B);
  xor XOR_2 (OR_out, A, B);
  nor nor_1 (nor_1_out, A, B);
  Adder #(.width(1)) adder_1 (.a(A), .b(xor_1_out), .out(adder_1_out), .cin(Cin), .cout(Cout));
  Multiplexer #(.select(3)) multiplexer_1 (
    .in0(AND_out), .in1(OR_out), .in2(OR_out), .in3(nor_1_out), .in4(adder_1_out), .out(Result),
    .sel(Operation));  // open: in5, in6, in7, en
endmodule

module _16_bits_ALU (
  input  [15:0] A,
  input  [15:0] B,
  input  Sub,
  input  [1:0] Operation,
  output [15:0] result,
  output Overflow,
  output Cout
);

  wire n1_bit_alu_1_cout, n1_bit_alu_2_cout, n1_bit_alu_3_cout, n1_bit_alu_4_cout, n1_bit_alu_5_cout,
       n1_bit_alu_6_cout, n1_bit_alu_7_cout, n1_bit_alu_8_cout, n1_bit_alu_9_cout, n1_bit_alu_10_cout,
       n1_bit_alu_11_cout, n1_bit_alu_12_cout, n1_bit_alu_13_cout, n1_bit_alu_14_cout, n1_bit_alu_15_cout;
  wire [2:2] undriven;

  _1_bit_ALU u_1_bit_alu_1 (
    .A(A[0]), .B(B[0]), .Result(result[0]), .Cin(Sub), .Sub(Sub), .Cout(n1_bit_alu_1_cout),
    .Operation({undriven[2], Operation}));
  _1_bit_ALU u_1_bit_alu_2 (
    .A(A[1]), .B(B[1]), .Result(result[1]), .Cin(n1_bit_alu_1_cout), .Sub(Sub), .Cout(n1_bit_alu_2_cout),
    .Operation({undriven[2], Operation}));
  _1_bit_ALU u_1_bit_alu_3 (
    .A(A[2]), .B(B[2]), .Result(result[2]), .Cin(n1_bit_alu_2_cout), .Sub(Sub), .Cout(n1_bit_alu_3_cout),
    .Operation({undriven[2], Operation}));
  _1_bit_ALU u_1_bit_alu_4 (
    .A(A[3]), .B(B[3]), .Result(result[3]), .Cin(n1_bit_alu_3_cout), .Sub(Sub), .Cout(n1_bit_alu_4_cout),
    .Operation({undriven[2], Operation}));
  _1_bit_ALU u_1_bit_alu_5 (
    .A(A[4]), .B(B[4]), .Result(result[4]), .Cin(n1_bit_alu_4_cout), .Sub(Sub), .Cout(n1_bit_alu_5_cout),
    .Operation({undriven[2], Operation}));
  _1_bit_ALU u_1_bit_alu_6 (
    .A(A[5]), .B(B[5]), .Result(result[5]), .Cin(n1_bit_alu_5_cout), .Sub(Sub), .Cout(n1_bit_alu_6_cout),
    .Operation({undriven[2], Operation}));
  _1_bit_ALU u_1_bit_alu_7 (
    .A(A[6]), .B(B[6]), .Result(result[6]), .Cin(n1_bit_alu_6_cout), .Sub(Sub), .Cout(n1_bit_alu_7_cout),
    .Operation({undriven[2], Operation}));
  _1_bit_ALU u_1_bit_alu_8 (
    .A(A[7]), .B(B[7]), .Result(result[7]), .Cin(n1_bit_alu_7_cout), .Sub(Sub), .Cout(n1_bit_alu_8_cout),
    .Operation({undriven[2], Operation}));
  _1_bit_ALU u_1_bit_alu_9 (
    .A(A[8]), .B(B[8]), .Result(result[8]), .Cin(n1_bit_alu_8_cout), .Sub(Sub), .Cout(n1_bit_alu_9_cout),
    .Operation({undriven[2], Operation}));
  _1_bit_ALU u_1_bit_alu_10 (
    .A(A[9]), .B(B[9]), .Result(result[9]), .Cin(n1_bit_alu_9_cout), .Sub(Sub), .Cout(n1_bit_alu_10_cout),
    .Operation({undriven[2], Operation}));
  _1_bit_ALU u_1_bit_alu_11 (
    .A(A[10]), .B(B[10]), .Result(result[10]), .Cin(n1_bit_alu_10_cout), .Sub(Sub),
    .Cout(n1_bit_alu_11_cout), .Operation({undriven[2], Operation}));
  _1_bit_ALU u_1_bit_alu_12 (
    .A(A[11]), .B(B[11]), .Result(result[11]), .Cin(n1_bit_alu_11_cout), .Sub(Sub),
    .Cout(n1_bit_alu_12_cout), .Operation({undriven[2], Operation}));
  _1_bit_ALU u_1_bit_alu_13 (
    .A(A[12]), .B(B[12]), .Result(result[12]), .Cin(n1_bit_alu_12_cout), .Sub(Sub),
    .Cout(n1_bit_alu_13_cout), .Operation({undriven[2], Operation}));
  _1_bit_ALU u_1_bit_alu_14 (
    .A(A[13]), .B(B[13]), .Result(result[13]), .Cin(n1_bit_alu_13_cout), .Sub(Sub),
    .Cout(n1_bit_alu_14_cout), .Operation({undriven[2], Operation}));
  _1_bit_ALU u_1_bit_alu_15 (
    .A(A[14]), .B(B[14]), .Result(result[14]), .Cin(n1_bit_alu_14_cout), .Sub(Sub),
    .Cout(n1_bit_alu_15_cout), .Operation({undriven[2], Operation}));
  _1_bit_ALU u_1_bit_alu_16 (
    .A(A[15]), .B(B[15]), .Result(result[15]), .Cin(n1_bit_alu_15_cout), .Sub(Sub), .Cout(Cout),
    .Operation({undriven[2], Operation}));
  xor xor_1 (Overflow, n1_bit_alu_15_cout, Cout);
  // Pins of 2 and 3 bits meet at {undriven[2], Operation}
endmodule
